# Fritzing sketch ConsoleAdapter (saved by Fritzing 0.9.5d)
stripboards: 1

parts:
  J1 = female pin header, 3 pins [form="♀ (female)"]
  J2 = male pin header, 6 pins [form="♂ (male)"]

nets:
  N1: J1.pin1, J2.pin1
  N2: J1.pin2, J2.pin5
  N3: J1.pin3, J2.pin4
