# Fritzing sketch TeensyJoystick_stripboard (saved by Fritzing 0.9.5d)
stripboards: 1

parts:
  Teensy_3_1 = Teensy 3.1
  Part1 = Adafruit Mini Analog Thumbstick [part_number="Adafruit #3246"]
  S1 = Pushbutton [package="[THT]"]
  S2 = Pushbutton [package="[THT]"]
  S3 = Pushbutton [package="[THT]"]
  LED1 = LED - 3mm [color="Green (565nm)" package="3 mm [THT]"]
  LED2 = LED - 3mm [color="Red (633nm)" package="3 mm [THT]"]
  R1 = Resistor [tolerance=±5% resistance=220 package=THT]
  R2 = Resistor [tolerance=±5% resistance=220 package=THT]

nets:
  GND: Teensy_3_1.GND, Teensy_3_1.AGND, Part1.GND, S1.Pin_3, S1.Pin_4, S2.Pin_3, S2.Pin_4, S3.Pin_3, S3.Pin_4, R1.Pin_0, R2.Pin_0
  N1: Teensy_3_1.D2, S3.Pin_1, S3.Pin_2
  N2: Teensy_3_1.D3, S2.Pin_1, S2.Pin_2
  N3: Teensy_3_1.D4, S1.Pin_1, S1.Pin_2
  N4: Teensy_3_1.D9, LED1.anode
  N5: Teensy_3_1.D10, LED2.anode
  N6: Teensy_3_1.3V3#15, Teensy_3_1.AREF, Part1.VCC
  N7: Teensy_3_1.A0/D14, Part1.YOUT
  N8: Teensy_3_1.A1/D15, Part1.XOUT
  N9: LED1.cathode, R1.Pin_1
  N10: LED2.cathode, R2.Pin_1

custom parts:
  Teensy 3.1: The Teensy is a complete USB-based microcontoller development system, in a very small footprint, capable of implementing many types of projects. All programming is done via the USB port. No special programmer is needed, only a standard micro-USB cable and a PC or Macintosh with a USB port. It has a USB keyboard/mouse/joystick emulation stack and can be programmed through Arduino IDE.
  Adafruit Mini Analog Thumbstick: Are you itching for an easy way to mount a PSP-like thumb joystick to your project? This Analog Mini Thumbstick Breakout Board will help you do just that! This is neat little PCB, on which you can mount a joystick/thumbstick -- we recommend this one. Since it's analog, you'll need two analog reading pins on your microcontroller to determine X and Y.
